# Fritzing sketch IRGlove (saved by Fritzing 0.9.3b)
breadboards: 1

parts:
  Onderdeel1 = Arduino Nano (Rev3.0)
  R1 = Resistor [tolerance=±5% resistance=330 package=THT]
  R2 = Resistor [tolerance=±5% resistance=10 package=THT]
  Q1 = NPN-Transistor [package="TO92 [THT]"]
  IR1 = TSOP312.., 314.. [package=THT]
  LED1 = LED - 5mm [color="Infrared (940nm)" package="5 mm [THT]"]
  BAT1 = BC9VPC [package=bc9vpc]

nets:
  N1: Onderdeel1.GND, Q1.C, IR1.Vs, BAT1.V-
  N2: Onderdeel1.D3, R1.Pin_0
  N3: Onderdeel1.D12/MISO, IR1.GND
  N4: Onderdeel1.VIN, BAT1.V+
  N5: Onderdeel1.5V, IR1.Data, LED1.anode
  N6: R1.Pin_1, Q1.B
  N7: R2.Pin_0, LED1.cathode
  N8: R2.Pin_1, Q1.E

notes:
  pink
  wijsvinger - forefinger
  middelvinger - middle finger
  ringvinger - ring finger
  Duim - Thumb
